// Logisim project 4-bit.circ as structural Verilog: 1 circuit, main circuit main
module main (
  input  [3:0] A,
  input  [3:0] B,
  input  [2:0] FS,
  output [3:0] RESULT
);

  wire adder_1_cout, comparator_1_eq, undriven;
  wire [3:0] adder_1_out, adder_2_out, and_1_out, not_1_out, not_2_out, or_1_out;

  DipSwitch #(.number(3)) dipswitch_1 ();  // open: sw1, sw2, sw3
  assign not_1_out = ~B;  // NOT_Gate not_1, 4 bits wide
  LED led_1 ();  // open: in
  Adder #(.width(4)) adder_1 (.a(A), .b(B), .out(adder_1_out), .cout(adder_1_cout));  // open: cin
  Adder #(.width(4)) adder_2 (.a(not_1_out), .b(A), .out(adder_2_out), .cin(undriven));  // open: cout
  assign and_1_out = A & B;  // AND_Gate and_1, 4 bits wide
  assign or_1_out = A | B;  // OR_Gate or_1, 4 bits wide
  assign not_2_out = ~A;  // NOT_Gate not_2, 4 bits wide
  Multiplexer #(.select(3), .width(4), .enable("false")) multiplexer_1 (
    .in0(adder_1_out), .in1(adder_2_out), .in2(and_1_out), .in3(or_1_out), .in4(not_2_out), .out(RESULT),
    .sel(FS));  // open: in5, in6, in7
  Comparator #(.width(4)) comparator_1 (.a(RESULT), .b(4'b0000), .eq(comparator_1_eq));  // open: gt, lt
  LED led_2 (.in(adder_1_cout));
  LED led_3 (.in(comparator_1_eq));
endmodule
